# Fritzing sketch Untitled Sketch 2 (saved by Fritzing 0.9.3b)
circuit board: 8.46667cm x 5.64444cm

parts:
  R1 = Resistor [tolerance=±5% resistance=10k package=THT]
  S1 = SWITCH-MOMENTARY-2 [package=tactile-pth-12mm]
  JP1 = Header 6 [package=molex-1x6-ra]  # not connected
  JP3 = Header 4 [package=screwterminal-3.5mm-4_lock]  # not connected
  JP4 = Header 2 [package=molex-1x2_lock]  # not connected

nets:
  N1: R1.Pin_1, S1.2
